# Fritzing sketch Ardularm (saved by Fritzing 0.9.3b)

parts:
  Part1 = Arduino Uno (Rev3)  # not connected
  Part2 = Arduino Ethernet Shield (Rev3)
  R-GND-G-B = RGB LED (com. cathode, rgb) [package="5 mm [THT]"]
  SDA-SCK-MOSI-MISO-(IRQ)-GND-RST-3_3V = RFID-RC522-v2
  GND-OUT-VCC = HC-SR501 Body Sensor Module

nets:
  N1: Part2.D8, SDA-SCK-MOSI-MISO-(IRQ)-GND-RST-3_3V.SDA
  N2: Part2.PWM_D9, R-GND-G-B.green_anode
  N3: Part2.PWM_D11, SDA-SCK-MOSI-MISO-(IRQ)-GND-RST-3_3V.MOSI
  N4: Part2.SPI/D12, SDA-SCK-MOSI-MISO-(IRQ)-GND-RST-3_3V.MISO
  N5: Part2.SPI/D13, SDA-SCK-MOSI-MISO-(IRQ)-GND-RST-3_3V.SCK
  GND: Part2.GND, R-GND-G-B.common_cathode, SDA-SCK-MOSI-MISO-(IRQ)-GND-RST-3_3V.GND, GND-OUT-VCC.GND
  N6: Part2.PWM_D3, R-GND-G-B.blue_anode
  N7: Part2.PWM_D5, SDA-SCK-MOSI-MISO-(IRQ)-GND-RST-3_3V.RST
  N8: Part2.PWM_D6, R-GND-G-B.red_anode
  N9: Part2.D7, GND-OUT-VCC.OUT
  3V3: Part2.3V3, SDA-SCK-MOSI-MISO-(IRQ)-GND-RST-3_3V.3.3V
  5V: Part2.5V, GND-OUT-VCC.VCC

custom parts:
  RFID-RC522-v2: A simple China made RFID-RC522 Reader; do check the pin labels, as this is a MFRC522 based clone.
  HC-SR501 Body Sensor Module: Pyroelectric Infrared PIR Motion Sensor Detector Module
